// Digital circuit inst-mem.dig as structural Verilog
module inst_mem (
  input  [8:0] ADDR,
  input  [4:0] PROG,
  output [31:0] IW
);

  wire [31:0] _00, _01, _02, _03, _04, _05, _06, _07, _08, _09, _10, _11, _12, _13, _14, _15, _16, _17, _18,
       _19, _20, _21, _22, _23, _24, _25, _26, _27, _28, _29, _30, _31;

  ROM #(.AddrBits(9), .Bits(32)) _00_unit_add_i (.A(ADDR), .sel(1'b1), .D(_00));
  ROM #(.AddrBits(9), .Bits(32)) _01_unit_add_r (.A(ADDR), .sel(1'b1), .D(_01));
  ROM #(.AddrBits(9), .Bits(32)) _02_unit_jal (.A(ADDR), .sel(1'b1), .D(_02));
  ROM #(.AddrBits(9), .Bits(32)) _03_unit_mul (.A(ADDR), .sel(1'b1), .D(_03));
  ROM #(.AddrBits(9), .Bits(32)) _04_unit_sll_r (.A(ADDR), .sel(1'b1), .D(_04));
  ROM #(.AddrBits(9), .Bits(32)) _05_unit_srl_r (.A(ADDR), .sel(1'b1), .D(_05));
  ROM #(.AddrBits(9), .Bits(32)) _06_unit_slli (.A(ADDR), .sel(1'b1), .D(_06));
  ROM #(.AddrBits(9), .Bits(32)) _07_unit_srli (.A(ADDR), .sel(1'b1), .D(_07));
  ROM #(.AddrBits(9), .Bits(32)) _08_unit_j (.A(ADDR), .sel(1'b1), .D(_08));
  ROM #(.AddrBits(9), .Bits(32)) _09_unit_beq (.A(ADDR), .sel(1'b1), .D(_09));
  ROM #(.AddrBits(9), .Bits(32)) _10_unit_blt (.A(ADDR), .sel(1'b1), .D(_10));
  ROM #(.AddrBits(9), .Bits(32)) _11_unit_bge (.A(ADDR), .sel(1'b1), .D(_11));
  ROM #(.AddrBits(9), .Bits(32)) _12_unit_sd_ld (.A(ADDR), .sel(1'b1), .D(_12));
  ROM #(.AddrBits(9), .Bits(32)) _13_unit_sw_lw (.A(ADDR), .sel(1'b1), .D(_13));
  ROM #(.AddrBits(9), .Bits(32)) _14_unit_sb_lb (.A(ADDR), .sel(1'b1), .D(_14));
  ROM #(.AddrBits(9), .Bits(32)) _15_prog_quadratic (.A(ADDR), .sel(1'b1), .D(_15));
  ROM #(.AddrBits(9), .Bits(32)) _16_prog_get_bitseq (.A(ADDR), .sel(1'b1), .D(_16));
  ROM #(.AddrBits(9), .Bits(32)) _17_prog_fibrec (.A(ADDR), .sel(1'b1), .D(_17));
  ROM #(.AddrBits(9), .Bits(32)) _18_prog_is_pal (.A(ADDR), .sel(1'b1), .D(_18));
  ROM #(.AddrBits(9), .Bits(32)) _19_prog_to_upper (.A(ADDR), .sel(1'b1), .D(_19));
  ROM #(.AddrBits(9), .Bits(32)) _20_prog_swap (.A(ADDR), .sel(1'b1), .D(_20));
  ROM #(.AddrBits(9), .Bits(32)) _21_prog_sort (.A(ADDR), .sel(1'b1), .D(_21));
  ROM #(.AddrBits(9), .Bits(32)) _22_prog_rstr (.A(ADDR), .sel(1'b1), .D(_22));
  ROM #(.AddrBits(9), .Bits(32)) _23_prog_countll (.A(ADDR), .sel(1'b1), .D(_23));
  ROM #(.AddrBits(9), .Bits(32)) _24_none (.A(ADDR), .sel(1'b1), .D(_24));
  ROM #(.AddrBits(9), .Bits(32)) _25_none (.A(ADDR), .sel(1'b1), .D(_25));
  ROM #(.AddrBits(9), .Bits(32)) _26_none (.A(ADDR), .sel(1'b1), .D(_26));
  ROM #(.AddrBits(9), .Bits(32)) _27_none (.A(ADDR), .sel(1'b1), .D(_27));
  ROM #(.AddrBits(9), .Bits(32)) _28_none (.A(ADDR), .sel(1'b1), .D(_28));
  ROM #(.AddrBits(9), .Bits(32)) _29_none (.A(ADDR), .sel(1'b1), .D(_29));
  ROM #(.AddrBits(9), .Bits(32)) _30_none (.A(ADDR), .sel(1'b1), .D(_30));
  ROM #(.AddrBits(9), .Bits(32)) _31_none (.A(ADDR), .sel(1'b1), .D(_31));
  Multiplexer #(.Selector_Bits(5), .Bits(32)) multiplexer_1 (
    .sel(PROG), .in_0(_00), .in_1(_01), .in_2(_02), .in_3(_03), .in_4(_04), .in_5(_05), .in_6(_06),
    .in_7(_07), .in_8(_08), .in_9(_09), .in_10(_10), .in_11(_11), .in_12(_12), .in_13(_13), .in_14(_14),
    .in_15(_15), .in_16(_16), .in_17(_17), .in_18(_18), .in_19(_19), .in_20(_20), .in_21(_21), .in_22(_22),
    .in_23(_23), .in_24(_24), .in_25(_25), .in_26(_26), .in_27(_27), .in_28(_28), .in_29(_29), .in_30(_30),
    .in_31(_31), .out(IW));

  // Notes on the sheet:
  //   contents of _00_unit_add_i (hex, n*v repeats v):
  //   00100513,00250513,c0001073
  //   contents of _01_unit_add_r (hex, n*v repeats v):
  //   00300513,00600593,00b50533,c0001073
  //   contents of _02_unit_jal (hex, n*v repeats v):
  //   00100513,00200593,008000ef,c0001073,00b50533,00008067
  //   contents of _03_unit_mul (hex, n*v repeats v):
  //   00300513,00700593,02b50533,c0001073
  //   contents of _04_unit_sll_r (hex, n*v repeats v):
  //   00100593,00200613,00c59533,c0001073
  //   contents of _05_unit_srl_r (hex, n*v repeats v):
  //   00800593,00100613,00c5d533,c0001073
  //   contents of _06_unit_slli (hex, n*v repeats v):
  //   00100593,00359513,c0001073
  //   contents of _07_unit_srli (hex, n*v repeats v):
  //   02000593,0025d513,c0001073
  //   contents of _08_unit_j (hex, n*v repeats v):
  //   00100513,0080006f,00000513,c0001073
  //   contents of _09_unit_beq (hex, n*v repeats v):
  //   00100513,00100593,00b50463,00000513,c0001073
  //   contents of _10_unit_blt (hex, n*v repeats v):
  //   00100513,00200593,00b54463,00000513,c0001073
  //   contents of _11_unit_bge (hex, n*v repeats v):
  //   00200513,00100593,00b55463,00000513,c0001073
  //   contents of _12_unit_sd_ld (hex, n*v repeats v):
  //   08000113,ff810113,00000513,06300293,00513023,00013503,c0001073
  //   contents of _13_unit_sw_lw (hex, n*v repeats v):
  //   08000113,ff810113,00000513,06300293,00512023,00012503,c0001073
  //   contents of _14_unit_sb_lb (hex, n*v repeats v):
  //   08000113,ff810113,00000513,06300293,005101a3,00310503,c0001073
  //   contents of _15_prog_quadratic (hex, n*v repeats v):
  //   00200513,00300593,00400613,00500693,008000ef,c0001073,02a502b3,02b282b3,02c50333,00628533,00d50533,
  //   00008067
  //   contents of _16_prog_get_bitseq (hex, n*v repeats v):
  //   00000513,01650513,00851513,0fa50513,00451513,00550513,00c00593,00f00613,008000ef,c0001073,40b602b3,
  //   00128293,04000393,00729863,00050313,fff00393,0140006f,00b55333,00100393,005393b3,fff38393,00737533,
  //   00008067
  //   contents of _17_prog_fibrec (hex, n*v repeats v):
  //   40000113,00a00513,008000ef,c0001073,00100293,00a2c463,00008067,fe810113,00113023,00a13423,fff50513,
  //   fe5ff0ef,00a13823,00813503,ffe50513,fd5ff0ef,01013303,00650533,00013083,01810113,00008067
  //   contents of _18_prog_is_pal (hex, n*v repeats v):
  //   40000113,ff810113,07200293,00510023,06100293,005100a3,06300293,00510123,06500293,005101a3,06300293,
  //   00510223,06100293,005102a3,07200293,00510323,000103a3,00200533,00000593,00600613,008000ef,c0001073,
  //   00c5c663,00100513,03c0006f,00b502b3,00028283,00c50333,00030303,00628663,00000513,0200006f,ff810113,
  //   00113023,00158593,fff60613,fc9ff0ef,00013083,00810113,00008067
  //   contents of _19_prog_to_upper (hex, n*v repeats v):
  //   40000113,ff810113,04600293,00510023,06f00293,005100a3,06f00293,00510123,04200293,005101a3,06100293,
  //   00510223,07200293,005102a3,00010323,00200533,ff810113,002005b3,002004b3,03c000ef,00000913,00000293,
  //   00800313,03800393,02628063,00048e03,007e1e33,01c96933,00148493,00128293,ff838393,fe5ff06f,01200533,
  //   c0001073,06100313,07b00393,00050283,02028063,0062c663,0072d463,fe028293,00558023,00150513,00158593,
  //   fe1ff06f,00058023,00008067
  //   contents of _20_prog_swap (hex, n*v repeats v):
  //   40000113,fe010113,00200293,00512023,00800293,00512223,00600293,00512423,00400293,00512623,00a00293,
  //   00512823,00c00293,00512a23,00200533,002004b3,00100593,00500613,018000ef,00412503,c0001073,00000013,
  //   00000013,00000013,00400293,02558333,00650333,025603b3,007503b3,00032e03,0003ae83,01d32023,01c3a023,
  //   00008067
  //   contents of _21_prog_sort (hex, n*v repeats v):
  //   40000113,fe010113,00200293,00512023,00800293,00512223,00600293,00512423,00400293,00512623,00a00293,
  //   00512823,00c00293,00512a23,00200533,002004b3,00400593,038000ef,0004a503,02051513,0044a283,00556533,
  //   0084a583,02059593,00c4a283,0055e5b3,0104a603,02061613,0144a283,00566633,c0001073,fd810113,00113023,
  //   00100293,06b2d263,00028313,04605a63,00400e13,03c30eb3,01d50f33,ffcf0f93,000f2f03,000faf83,03ff5c63,
  //   00a13423,00b13823,00513c23,02613023,00030593,fff30613,030000ef,00813503,01013583,01813283,02013303,
  //   fff30313,fb1ff06f,00128293,fa1ff06f,00013083,02810113,00008067,00400293,02558333,00650333,025603b3,
  //   007503b3,00032e03,0003ae83,01d32023,01c3a023,00008067
  //   contents of _22_prog_rstr (hex, n*v repeats v):
  //   40000113,ff810113,04600293,00510023,06f00293,005100a3,06f00293,00510123,04200293,005101a3,06100293,
  //   00510223,07200293,005102a3,00010323,000103a3,002005b3,ff810113,00200533,002004b3,05c000ef,00000913,
  //   00000293,00800313,03800393,02628063,00048e03,007e1e33,01c96933,00148493,00128293,ff838393,fe5ff06f,
  //   01200533,c0001073,00000293,00050303,00030863,00128293,00150513,ff1ff06f,00028513,00008067,fe010113,
  //   00113023,00a13423,00b13823,00058513,fcdff0ef,00050293,00813503,01013583,00000313,00028393,fff38393,
  //   02535063,00758eb3,000e8f03,00650eb3,01ee8023,00130313,fff38393,fe5ff06f,00000f13,00550eb3,01ee8023,
  //   00013083,02010113,00008067
  //   contents of _23_prog_countll (hex, n*v repeats v):
  //   40000113,fd010113,00b00293,00512423,01010293,00513023,01600293,00512c23,02010293,00513823,01600293,
  //   02512423,00000293,02513023,00200533,008000ef,c0001073,00000293,00050863,00128293,00053503,ff5ff06f,
  //   00028513,00008067
  //   contents of _24_none (hex, n*v repeats v):
  //   deadbeef
  //   contents of _25_none (hex, n*v repeats v):
  //   deadbeef
  //   contents of _26_none (hex, n*v repeats v):
  //   deadbeef
  //   contents of _27_none (hex, n*v repeats v):
  //   deadbeef
  //   contents of _28_none (hex, n*v repeats v):
  //   deadbeef
  //   contents of _29_none (hex, n*v repeats v):
  //   deadbeef
  //   contents of _30_none (hex, n*v repeats v):
  //   deadbeef
  //   contents of _31_none (hex, n*v repeats v):
  //   deadbeef
endmodule
